// Logisim project cpu.circ as structural Verilog: 24 circuits, main circuit main
module main (
  input  [31:0] INSTRUCTION,
  input  CLOCK,
  output [31:0] PROGRAM_COUNTER,
  output [31:0] ra,
  output [31:0] sp,
  output [31:0] t0,
  output [31:0] t1,
  output [31:0] t2,
  output [31:0] s0,
  output [31:0] s1,
  output [31:0] a0
);

  wire ASel, BrEq, BrLT, BrUn, BSel, MemRW, PCSel, RegWEn;
  wire [1:0] LoadSel, Offset, WBSel;
  wire [2:0] ImmSel;
  wire [3:0] ALUSel;
  wire [4:0] rd, rs1, rs2;
  wire [31:0] adder_1_out, ALUOut, imm, instID, LoadData, MemData, multiplexer_1_out, multiplexer_2_out,
       multiplexer_3_out, multiplexer_4_out, PCID, PCPlus4, rs1Out, rs2Out, wb;
  wire [31:2] divider_1_rem;

  Adder #(.width(32)) adder_1 (.a(PROGRAM_COUNTER), .b(32'h4), .out(adder_1_out));  // open: cin, cout
  Multiplexer #(.width(32), .enable("false")) multiplexer_1 (
    .in0(adder_1_out), .in1(ALUOut), .out(multiplexer_1_out), .sel(PCSel));
  Register #(.width(32)) register_1 (.D(multiplexer_2_out), .clk(CLOCK), .Q(instID));  // open: en, clr
  Multiplexer #(.width(32), .enable("false")) multiplexer_2 (
    .in0(INSTRUCTION), .in1(32'h13), .out(multiplexer_2_out), .sel(PCSel));
  Register #(.width(32)) register_2 (.D(PROGRAM_COUNTER), .clk(CLOCK), .Q(PCID));  // open: en, clr
  Register #(.width(32)) PC (.D(multiplexer_1_out), .clk(CLOCK), .Q(PROGRAM_COUNTER));  // open: en, clr
  Adder #(.width(32)) adder_2 (.a(PCID), .b(32'h4), .out(PCPlus4));  // open: cin, cout
  ImmRsdDecoder immrsddecoder_1 (
    .Instruction(instID), .rd(rd), .rs1(rs1), .rs2(rs2));  // open: immI, immS, immB, immU, immJ
  ImmGen immgen_1 (.Instruction(instID), .ImmSel(ImmSel), .clk(CLOCK), .imm(imm));
  regfile_main main_1 (
    .rs2(rs2), .rd(rd), .Read_Data_1(rs1Out), .Read_Data_2(rs2Out), .ra(ra), .sp(sp), .t0(t0), .t1(t1),
    .t2(t2), .s0(s0), .s1(s1), .a0(a0), .rs1(rs1), .Write_Data(wb), .RegWEn(RegWEn), .clk(CLOCK));
  Multiplexer #(.width(32), .enable("false")) multiplexer_3 (
    .in0(rs1Out), .in1(PCID), .out(multiplexer_3_out), .sel(ASel));
  Multiplexer #(.width(32), .enable("false")) multiplexer_4 (
    .in0(rs2Out), .in1(imm), .out(multiplexer_4_out), .sel(BSel));
  alu alu_1 (.B(multiplexer_4_out), .Result(ALUOut), .A(multiplexer_3_out), .ALUSel(ALUSel));
  BrCmp brcmp_1 (.rs1(rs1Out), .rs2(rs2Out), .BrUn(BrUn), .BrEq(BrEq), .BrLt(BrLT));
  Control control_1 (
    .Instruction(instID), .BrEq(BrEq), .BrLt(BrLT), .PCSel(PCSel), .RegWEn(RegWEn), .ImmSel(ImmSel),
    .BrUn(BrUn), .BSel(BSel), .ASel(ASel), .ALUSel(ALUSel), .MemRW(MemRW), .WBSel(WBSel), .LoadSel(LoadSel));
  Divider #(.width(32)) divider_1 (.a(ALUOut), .b(32'h4), .rem({divider_1_rem, Offset}));  // open: out, upper
  Multiplexer #(.select(2), .width(32), .enable("false")) multiplexer_5 (
    .in0(PCPlus4), .in1(ALUOut), .in2(LoadData), .out(wb), .sel(WBSel));  // open: in3
  // mem_main main_2: pin names not known; wires that end beside it: ALUOut, rs2Out, CLOCK, MemRW, MemData
  LoadExtender loadextender_1 (.MemData(MemData), .LoadSel(LoadSel), .Offset(Offset), .LoadData(LoadData));

  // Other names for the same wires on the sheet: clk = CLOCK; PC[31:0] = PROGRAM_COUNTER

  // Notes on the sheet:
  //   Output
  //   Part of Instruction Fetch
  //   Two-Stage Pipelining
  //   IMEM (do **NOT** move this)
  //   Inputs
  //   Instruction Decode
  //   Inputs/Outputs for testing. Do **NOT** move these.
  //   Execute
  //   Memory
  //   Writeback
endmodule

module BrCmp (
  input  [31:0] rs1,
  input  [31:0] rs2,
  input  BrUn,
  output BrEq,
  output BrLt
);

  wire comparator_1_eq, comparator_1_lt, comparator_2_eq, comparator_2_lt;

  Comparator #(.width(32)) comparator_1 (.a(rs1), .b(rs2), .eq(comparator_1_eq), .lt(comparator_1_lt));  // open: gt
  Comparator #(.width(32), .mode("unsigned")) comparator_2 (
    .a(rs1), .b(rs2), .eq(comparator_2_eq), .lt(comparator_2_lt));  // open: gt
  Multiplexer #(.enable("false")) multiplexer_1 (.in0(comparator_1_eq), .in1(comparator_2_eq), .out(BrEq), .sel(BrUn));
  Multiplexer #(.enable("false")) multiplexer_2 (.in0(comparator_1_lt), .in1(comparator_2_lt), .out(BrLt), .sel(BrUn));

  // Other names for the same wires on the sheet: A[31:0] = rs1; B[31:0] = rs2; isUnsigned = BrUn
endmodule

module ImmGen (
  input  [31:0] Instruction,
  input  [2:0] ImmSel,
  input  clk,
  output [31:0] imm
);

  wire [11:0] immI, immS;
  wire [12:0] immB;
  wire [20:0] immJ;
  wire [31:0] B, I, immU, J, S;

  ImmRsdDecoder immrsddecoder_1 (
    .Instruction(Instruction), .immI(immI), .immS(immS), .immB(immB), .immU(immU), .immJ(immJ));  // open: rd, rs1, rs2
  assign I = {{20{immI[11]}}, immI};  // Bit_Extender bit_extender_1
  assign S = {{20{immS[11]}}, immS};  // Bit_Extender bit_extender_2
  assign B = {{19{immB[12]}}, immB};  // Bit_Extender bit_extender_3
  assign J = {{11{immJ[20]}}, immJ};  // Bit_Extender bit_extender_4
  Multiplexer #(.select(3), .width(32), .enable("false")) multiplexer_1 (
    .in0(I), .in1(S), .in2(B), .in3(immU), .in4(J), .out(imm), .sel(ImmSel));  // open: in5, in6, in7

  // Other names for the same wires on the sheet: inst[31:0] = Instruction
endmodule

module LoadExtender (
  input  [31:0] MemData,
  input  [1:0] LoadSel,
  input  [1:0] Offset,
  output [31:0] LoadData
);

  wire [7:0] ByteData;
  wire [15:0] HalfData;
  wire [31:0] bit_extender_1_out, bit_extender_2_out;

  assign bit_extender_1_out = {{24{ByteData[7]}}, ByteData};  // Bit_Extender bit_extender_1
  assign bit_extender_2_out = {{16{HalfData[15]}}, HalfData};  // Bit_Extender bit_extender_2
  Multiplexer #(.select(2), .width(8), .enable("false")) multiplexer_1 (
    .in0(MemData[7:0]), .in1(MemData[15:8]), .in2(MemData[23:16]), .in3(MemData[31:24]), .out(ByteData),
    .sel(Offset));
  Multiplexer #(.select(2), .width(16), .enable("false")) multiplexer_2 (
    .in0(MemData[15:0]), .in2(MemData[31:16]), .out(HalfData), .sel(Offset));  // open: in1, in3
  Multiplexer #(.select(2), .width(32), .enable("false")) multiplexer_3 (
    .in0(bit_extender_1_out), .in1(bit_extender_2_out), .in2(MemData), .out(LoadData), .sel(LoadSel));  // open: in3

  // Notes on the sheet:
  //   LoadSel: 0=lb,1=lh,2=lw
  //   Currently only supports 0,1,2
endmodule

module ImmRsdDecoder (
  input  [31:0] Instruction,
  output [4:0] rd,
  output [4:0] rs1,
  output [4:0] rs2,
  output [11:0] immI,
  output [11:0] immS,
  output [12:0] immB,
  output [31:0] immU,
  output [20:0] immJ
);


  assign immB = {Instruction[31], Instruction[7], Instruction[30:25], Instruction[11:8], 1'b0};
  assign immI = Instruction[31:20];
  assign immJ = {Instruction[31], Instruction[19:12], Instruction[20], Instruction[30:21], 1'b0};
  assign immS = {Instruction[31:25], Instruction[11:7]};
  assign immU = {Instruction[31:12], {12{1'b0}}};
  assign rd = Instruction[11:7];
  assign rs1 = Instruction[19:15];
  assign rs2 = Instruction[24:20];

  // Other names for the same wires on the sheet: inst[31:0] = Instruction
endmodule

module OpcodeFunctDecoder (
  input  [31:0] Instruction,
  output [6:0] Opcode,
  output [2:0] Funct3,
  output [6:0] Funct7
);


  assign Funct3 = Instruction[14:12];
  assign Funct7 = Instruction[31:25];
  assign Opcode = Instruction[6:0];
endmodule

module Control (
  input  [31:0] Instruction,
  input  BrEq,
  input  BrLt,
  output PCSel,
  output RegWEn,
  output [2:0] ImmSel,
  output BrUn,
  output BSel,
  output ASel,
  output [3:0] ALUSel,
  output MemRW,
  output [1:0] WBSel,
  output [1:0] LoadSel
);

  PCSel_0 pcsel_0_1 (.Instruction(Instruction), .BrEq(BrEq), .BrLt(BrLt), .PCSel(PCSel));
  ALUSel_0 alusel_0_1 (.Instruction(Instruction), .ALUSel_0(ALUSel[0]));
  ALUSel_1 alusel_1_1 (.Instruction(Instruction), .ALUSel_1(ALUSel[1]));
  ALUSel_2 alusel_2_1 (.Instruction(Instruction), .ALUSel_2(ALUSel[2]));
  ALUSel_3 alusel_3_1 (.Instruction(Instruction), .ALUSel_3(ALUSel[3]));
  RegWEn_0 regwen_0_1 (.Instruction(Instruction), .RegWEn(RegWEn));
  ImmSel_0 immsel_0_1 (.Instruction(Instruction), .ImmSel_0(ImmSel[0]));
  ImmSel_1 immsel_1_1 (.Instruction(Instruction), .ImmSel_1(ImmSel[1]));
  ImmSel_2 immsel_2_1 (.Instruction(Instruction), .ImmSel_2(ImmSel[2]));
  BrUn_0 brun_0_1 (.Instruction(Instruction), .BrUn(BrUn));
  ASel_0 asel_0_1 (.Instruction(Instruction), .ASel(ASel));
  BSel_0 bsel_0_1 (.Instruction(Instruction), .BSel(BSel));
  MemRW_0 memrw_0_1 (.Instruction(Instruction), .MemRW(MemRW));
  WBSel_0 wbsel_0_1 (.Instruction(Instruction), .WBSel_0(WBSel[0]));
  WBSel_1 wbsel_1_1 (.Instruction(Instruction), .WBSel_1(WBSel[1]));
  LoadSel_0 loadsel_0_1 (.Instruction(Instruction), .LoadSel_0(LoadSel[0]));
  LoadSel_1 loadsel_1_1 (.Instruction(Instruction), .LoadSel_1(LoadSel[1]));

  // Other names for the same wires on the sheet: inst[31:0] = Instruction
endmodule

module ALUSel_3 (
  input  [31:0] Instruction,
  output ALUSel_3
);

  wire comparator_1_eq, comparator_2_eq, comparator_3_eq, comparator_4_eq, comparator_5_eq, comparator_6_eq,
       comparator_7_eq, comparator_8_eq, comparator_9_eq, comparator_10_eq, comparator_11_eq,
       comparator_12_eq, comparator_13_eq, comparator_14_eq, comparator_15_eq, comparator_16_eq,
       comparator_17_eq, comparator_18_eq, divu, lui, mul, mulh, mulhu, remu, sub;
  wire [2:0] Funct3;
  wire [6:0] Funct7, Opcode;

  OpcodeFunctDecoder opcodefunctdecoder_1 (
    .Instruction(Instruction), .Opcode(Opcode), .Funct3(Funct3), .Funct7(Funct7));
  Comparator #(.width(7)) comparator_1 (.a(Opcode), .b(7'b0110011), .eq(comparator_1_eq));  // open: gt, lt
  Comparator #(.width(3)) comparator_2 (.a(Funct3), .b(3'b000), .eq(comparator_2_eq));  // open: gt, lt
  Comparator #(.width(7)) comparator_3 (.a(Funct7), .b(7'b0000001), .eq(comparator_3_eq));  // open: gt, lt
  Comparator #(.width(7)) comparator_4 (.a(Opcode), .b(7'b0110011), .eq(comparator_4_eq));  // open: gt, lt
  Comparator #(.width(3)) comparator_5 (.a(Funct3), .b(3'b000), .eq(comparator_5_eq));  // open: gt, lt
  Comparator #(.width(7)) comparator_6 (.a(Funct7), .b(7'b0100000), .eq(comparator_6_eq));  // open: gt, lt
  Comparator #(.width(7)) comparator_7 (.a(Opcode), .b(7'b0110011), .eq(comparator_7_eq));  // open: gt, lt
  Comparator #(.width(3)) comparator_8 (.a(Funct3), .b(3'b001), .eq(comparator_8_eq));  // open: gt, lt
  Comparator #(.width(7)) comparator_9 (.a(Funct7), .b(7'b0000001), .eq(comparator_9_eq));  // open: gt, lt
  Comparator #(.width(7)) comparator_10 (.a(Opcode), .b(7'b0110011), .eq(comparator_10_eq));  // open: gt, lt
  Comparator #(.width(3)) comparator_11 (.a(Funct3), .b(3'b011), .eq(comparator_11_eq));  // open: gt, lt
  Comparator #(.width(7)) comparator_12 (.a(Funct7), .b(7'b0000001), .eq(comparator_12_eq));  // open: gt, lt
  and and_1 (mul, comparator_1_eq, comparator_2_eq, comparator_3_eq);
  and and_2 (sub, comparator_4_eq, comparator_5_eq, comparator_6_eq);
  and and_3 (mulh, comparator_7_eq, comparator_8_eq, comparator_9_eq);
  and and_4 (mulhu, comparator_10_eq, comparator_11_eq, comparator_12_eq);
  Comparator #(.width(7)) comparator_13 (.a(Opcode), .b(7'b0110011), .eq(comparator_13_eq));  // open: gt, lt
  Comparator #(.width(3)) comparator_14 (.a(Funct3), .b(3'b101), .eq(comparator_14_eq));  // open: gt, lt
  Comparator #(.width(7)) comparator_15 (.a(Funct7), .b(7'b0000001), .eq(comparator_15_eq));  // open: gt, lt
  Comparator #(.width(7)) comparator_16 (.a(Opcode), .b(7'b0110011), .eq(comparator_16_eq));  // open: gt, lt
  Comparator #(.width(3)) comparator_17 (.a(Funct3), .b(3'b111), .eq(comparator_17_eq));  // open: gt, lt
  Comparator #(.width(7)) comparator_18 (.a(Funct7), .b(7'b0000001), .eq(comparator_18_eq));  // open: gt, lt
  Comparator #(.width(7)) comparator_19 (.a(Opcode), .b(7'b0110111), .eq(lui));  // open: gt, lt
  and and_5 (divu, comparator_13_eq, comparator_14_eq, comparator_15_eq);
  and and_6 (remu, comparator_16_eq, comparator_17_eq, comparator_18_eq);
  or or_1 (ALUSel_3, mul, sub, mulh, mulhu, divu, remu, lui);

  // Other names for the same wires on the sheet: inst[31:0] = Instruction
endmodule

module ALUSel_2 (
  input  [31:0] Instruction,
  output ALUSel_2
);

  wire comparator_1_eq, comparator_2_eq, comparator_3_eq, comparator_4_eq, comparator_5_eq, comparator_6_eq,
       comparator_7_eq, comparator_8_eq, comparator_9_eq, comparator_10_eq, comparator_11_eq,
       comparator_12_eq, comparator_13_eq, comparator_14_eq, comparator_15_eq, comparator_16_eq,
       comparator_17_eq, comparator_18_eq, comparator_19_eq, comparator_20_eq, comparator_21_eq,
       comparator_22_eq, comparator_23_eq, comparator_24_eq, comparator_26_eq, comparator_27_eq,
       comparator_28_eq, comparator_29_eq, comparator_30_eq, lui, mulh, sll_1, slli, slt, slti, sra_1, srai,
       srl_1, srli, sub;
  wire [2:0] Funct3;
  wire [6:0] Funct7, Opcode;

  OpcodeFunctDecoder opcodefunctdecoder_1 (
    .Instruction(Instruction), .Opcode(Opcode), .Funct3(Funct3), .Funct7(Funct7));
  Comparator #(.width(7)) comparator_1 (.a(Opcode), .b(7'b0110011), .eq(comparator_1_eq));  // open: gt, lt
  Comparator #(.width(3)) comparator_2 (.a(Funct3), .b(3'b000), .eq(comparator_2_eq));  // open: gt, lt
  Comparator #(.width(7)) comparator_3 (.a(Funct7), .b(7'b0100000), .eq(comparator_3_eq));  // open: gt, lt
  Comparator #(.width(7)) comparator_4 (.a(Opcode), .b(7'b0110011), .eq(comparator_4_eq));  // open: gt, lt
  Comparator #(.width(3)) comparator_5 (.a(Funct3), .b(3'b001), .eq(comparator_5_eq));  // open: gt, lt
  Comparator #(.width(7)) comparator_6 (.a(Funct7), .b(7'b0000001), .eq(comparator_6_eq));  // open: gt, lt
  Comparator #(.width(7)) comparator_7 (.a(Opcode), .b(7'b0110011), .eq(comparator_7_eq));  // open: gt, lt
  Comparator #(.width(3)) comparator_8 (.a(Funct3), .b(3'b001), .eq(comparator_8_eq));  // open: gt, lt
  Comparator #(.width(7)) comparator_9 (.a(Funct7), .b({7{1'b0}}), .eq(comparator_9_eq));  // open: gt, lt
  Comparator #(.width(7)) comparator_10 (.a(Opcode), .b(7'b0110011), .eq(comparator_10_eq));  // open: gt, lt
  Comparator #(.width(3)) comparator_11 (.a(Funct3), .b(3'b101), .eq(comparator_11_eq));  // open: gt, lt
  Comparator #(.width(7)) comparator_12 (.a(Funct7), .b({7{1'b0}}), .eq(comparator_12_eq));  // open: gt, lt
  and and_1 (sub, comparator_1_eq, comparator_2_eq, comparator_3_eq);
  and and_2 (mulh, comparator_4_eq, comparator_5_eq, comparator_6_eq);
  and and_3 (sll_1, comparator_7_eq, comparator_8_eq, comparator_9_eq);
  and and_4 (srl_1, comparator_10_eq, comparator_11_eq, comparator_12_eq);
  Comparator #(.width(7)) comparator_13 (.a(Opcode), .b(7'b0010011), .eq(comparator_13_eq));  // open: gt, lt
  Comparator #(.width(3)) comparator_14 (.a(Funct3), .b(3'b001), .eq(comparator_14_eq));  // open: gt, lt
  Comparator #(.width(7)) comparator_15 (.a(Funct7), .b({7{1'b0}}), .eq(comparator_15_eq));  // open: gt, lt
  Comparator #(.width(7)) comparator_16 (.a(Opcode), .b(7'b0110011), .eq(comparator_16_eq));  // open: gt, lt
  Comparator #(.width(3)) comparator_17 (.a(Funct3), .b(3'b101), .eq(comparator_17_eq));  // open: gt, lt
  Comparator #(.width(7)) comparator_18 (.a(Funct7), .b(7'b0100000), .eq(comparator_18_eq));  // open: gt, lt
  Comparator #(.width(7)) comparator_19 (.a(Opcode), .b(7'b0110011), .eq(comparator_19_eq));  // open: gt, lt
  Comparator #(.width(3)) comparator_20 (.a(Funct3), .b(3'b010), .eq(comparator_20_eq));  // open: gt, lt
  Comparator #(.width(7)) comparator_21 (.a(Funct7), .b({7{1'b0}}), .eq(comparator_21_eq));  // open: gt, lt
  Comparator #(.width(7)) comparator_22 (.a(Opcode), .b(7'b0010011), .eq(comparator_22_eq));  // open: gt, lt
  Comparator #(.width(3)) comparator_23 (.a(Funct3), .b(3'b101), .eq(comparator_23_eq));  // open: gt, lt
  Comparator #(.width(7)) comparator_24 (.a(Funct7), .b(7'b0100000), .eq(comparator_24_eq));  // open: gt, lt
  and and_5 (slli, comparator_13_eq, comparator_14_eq, comparator_15_eq);
  and and_6 (sra_1, comparator_16_eq, comparator_17_eq, comparator_18_eq);
  and and_7 (slt, comparator_19_eq, comparator_20_eq, comparator_21_eq);
  and and_8 (srai, comparator_22_eq, comparator_23_eq, comparator_24_eq);
  or or_1 (ALUSel_2, mulh, sll_1, srl_1, slli, sra_1, sub, slt, srai, slti, srli, lui);
  Comparator #(.width(7)) comparator_25 (.a(Opcode), .b(7'b0110111), .eq(lui));  // open: gt, lt
  Comparator #(.width(7)) comparator_26 (.a(Opcode), .b(7'b0010011), .eq(comparator_26_eq));  // open: gt, lt
  Comparator #(.width(3)) comparator_27 (.a(Funct3), .b(3'b010), .eq(comparator_27_eq));  // open: gt, lt
  Comparator #(.width(7)) comparator_28 (.a(Opcode), .b(7'b0010011), .eq(comparator_28_eq));  // open: gt, lt
  Comparator #(.width(3)) comparator_29 (.a(Funct3), .b(3'b101), .eq(comparator_29_eq));  // open: gt, lt
  Comparator #(.width(7)) comparator_30 (.a(Funct7), .b({7{1'b0}}), .eq(comparator_30_eq));  // open: gt, lt
  and and_9 (slti, comparator_26_eq, comparator_27_eq);
  and and_10 (srli, comparator_28_eq, comparator_29_eq, comparator_30_eq);

  // Other names for the same wires on the sheet: inst[31:0] = Instruction
endmodule

module ALUSel_1 (
  input  [31:0] Instruction,
  output ALUSel_1
);

  wire comparator_1_eq, comparator_2_eq, comparator_3_eq, comparator_4_eq, comparator_5_eq, comparator_6_eq,
       comparator_7_eq, comparator_8_eq, comparator_9_eq, comparator_10_eq, comparator_11_eq,
       comparator_12_eq, comparator_13_eq, comparator_14_eq, comparator_15_eq, comparator_16_eq,
       comparator_17_eq, comparator_18_eq, comparator_19_eq, comparator_20_eq, comparator_21_eq,
       comparator_22_eq, comparator_23_eq, comparator_24_eq, comparator_25_eq, comparator_26_eq,
       comparator_27_eq, comparator_28_eq, comparator_29_eq, comparator_30_eq, mul, mulh, mulhu, or_1, ori,
       sll_1, slli, slt, slti, xor_1, xori;
  wire [2:0] Funct3;
  wire [6:0] Funct7, Opcode;

  OpcodeFunctDecoder opcodefunctdecoder_1 (
    .Instruction(Instruction), .Opcode(Opcode), .Funct3(Funct3), .Funct7(Funct7));
  Comparator #(.width(7)) comparator_1 (.a(Opcode), .b(7'b0110011), .eq(comparator_1_eq));  // open: gt, lt
  Comparator #(.width(3)) comparator_2 (.a(Funct3), .b(3'b000), .eq(comparator_2_eq));  // open: gt, lt
  Comparator #(.width(7)) comparator_3 (.a(Funct7), .b(7'b0000001), .eq(comparator_3_eq));  // open: gt, lt
  Comparator #(.width(7)) comparator_4 (.a(Opcode), .b(7'b0110011), .eq(comparator_4_eq));  // open: gt, lt
  Comparator #(.width(3)) comparator_5 (.a(Funct3), .b(3'b001), .eq(comparator_5_eq));  // open: gt, lt
  Comparator #(.width(7)) comparator_6 (.a(Funct7), .b({7{1'b0}}), .eq(comparator_6_eq));  // open: gt, lt
  Comparator #(.width(7)) comparator_7 (.a(Opcode), .b(7'b0110011), .eq(comparator_7_eq));  // open: gt, lt
  Comparator #(.width(3)) comparator_8 (.a(Funct3), .b(3'b001), .eq(comparator_8_eq));  // open: gt, lt
  Comparator #(.width(7)) comparator_9 (.a(Funct7), .b(7'b0000001), .eq(comparator_9_eq));  // open: gt, lt
  Comparator #(.width(7)) comparator_10 (.a(Opcode), .b(7'b0110011), .eq(comparator_10_eq));  // open: gt, lt
  Comparator #(.width(3)) comparator_11 (.a(Funct3), .b(3'b010), .eq(comparator_11_eq));  // open: gt, lt
  Comparator #(.width(7)) comparator_12 (.a(Funct7), .b({7{1'b0}}), .eq(comparator_12_eq));  // open: gt, lt
  and and_1 (mul, comparator_1_eq, comparator_2_eq, comparator_3_eq);
  and and_2 (sll_1, comparator_4_eq, comparator_5_eq, comparator_6_eq);
  and and_3 (mulh, comparator_7_eq, comparator_8_eq, comparator_9_eq);
  and and_4 (slt, comparator_10_eq, comparator_11_eq, comparator_12_eq);
  Comparator #(.width(7)) comparator_13 (.a(Opcode), .b(7'b0110011), .eq(comparator_13_eq));  // open: gt, lt
  Comparator #(.width(3)) comparator_14 (.a(Funct3), .b(3'b011), .eq(comparator_14_eq));  // open: gt, lt
  Comparator #(.width(7)) comparator_15 (.a(Funct7), .b(7'b0000001), .eq(comparator_15_eq));  // open: gt, lt
  Comparator #(.width(7)) comparator_16 (.a(Opcode), .b(7'b0110011), .eq(comparator_16_eq));  // open: gt, lt
  Comparator #(.width(3)) comparator_17 (.a(Funct3), .b(3'b100), .eq(comparator_17_eq));  // open: gt, lt
  Comparator #(.width(7)) comparator_18 (.a(Funct7), .b({7{1'b0}}), .eq(comparator_18_eq));  // open: gt, lt
  Comparator #(.width(7)) comparator_19 (.a(Opcode), .b(7'b0110011), .eq(comparator_19_eq));  // open: gt, lt
  Comparator #(.width(3)) comparator_20 (.a(Funct3), .b(3'b110), .eq(comparator_20_eq));  // open: gt, lt
  Comparator #(.width(7)) comparator_21 (.a(Funct7), .b({7{1'b0}}), .eq(comparator_21_eq));  // open: gt, lt
  Comparator #(.width(7)) comparator_22 (.a(Opcode), .b(7'b0010011), .eq(comparator_22_eq));  // open: gt, lt
  Comparator #(.width(3)) comparator_23 (.a(Funct3), .b(3'b001), .eq(comparator_23_eq));  // open: gt, lt
  Comparator #(.width(7)) comparator_24 (.a(Funct7), .b({7{1'b0}}), .eq(comparator_24_eq));  // open: gt, lt
  and and_5 (mulhu, comparator_13_eq, comparator_14_eq, comparator_15_eq);
  and and_6 (xor_1, comparator_16_eq, comparator_17_eq, comparator_18_eq);
  and and_7 (or_1, comparator_19_eq, comparator_20_eq, comparator_21_eq);
  and and_8 (slli, comparator_22_eq, comparator_23_eq, comparator_24_eq);
  Comparator #(.width(7)) comparator_25 (.a(Opcode), .b(7'b0010011), .eq(comparator_25_eq));  // open: gt, lt
  Comparator #(.width(3)) comparator_26 (.a(Funct3), .b(3'b010), .eq(comparator_26_eq));  // open: gt, lt
  Comparator #(.width(7)) comparator_27 (.a(Opcode), .b(7'b0010011), .eq(comparator_27_eq));  // open: gt, lt
  Comparator #(.width(3)) comparator_28 (.a(Funct3), .b(3'b100), .eq(comparator_28_eq));  // open: gt, lt
  Comparator #(.width(7)) comparator_29 (.a(Opcode), .b(7'b0010011), .eq(comparator_29_eq));  // open: gt, lt
  Comparator #(.width(3)) comparator_30 (.a(Funct3), .b(3'b110), .eq(comparator_30_eq));  // open: gt, lt
  or u_or_1 (ALUSel_1, mul, sll_1, mulh, slt, mulhu, xor_1, or_1, slli, slti, xori, ori);
  and and_9 (slti, comparator_25_eq, comparator_26_eq);
  and and_10 (xori, comparator_27_eq, comparator_28_eq);
  and and_11 (ori, comparator_29_eq, comparator_30_eq);

  // Other names for the same wires on the sheet: inst[31:0] = Instruction
endmodule

module ALUSel_0 (
  input  [31:0] Instruction,
  output ALUSel_0
);

  wire and_1, andi, comparator_1_eq, comparator_2_eq, comparator_3_eq, comparator_4_eq, comparator_5_eq,
       comparator_6_eq, comparator_7_eq, comparator_8_eq, comparator_9_eq, comparator_10_eq,
       comparator_11_eq, comparator_12_eq, comparator_13_eq, comparator_14_eq, comparator_15_eq,
       comparator_16_eq, comparator_17_eq, comparator_18_eq, comparator_19_eq, comparator_20_eq,
       comparator_21_eq, comparator_24_eq, comparator_25_eq, comparator_26_eq, comparator_27_eq,
       comparator_28_eq, comparator_29_eq, jal, lui, mulhu, remu, slt, slti, sra_1, srai, xor_1, xori;
  wire [2:0] Funct3;
  wire [6:0] Funct7, Opcode;

  OpcodeFunctDecoder opcodefunctdecoder_1 (
    .Instruction(Instruction), .Opcode(Opcode), .Funct3(Funct3), .Funct7(Funct7));
  Comparator #(.width(7)) comparator_1 (.a(Opcode), .b(7'b0110011), .eq(comparator_1_eq));  // open: gt, lt
  Comparator #(.width(3)) comparator_2 (.a(Funct3), .b(3'b010), .eq(comparator_2_eq));  // open: gt, lt
  Comparator #(.width(7)) comparator_3 (.a(Funct7), .b({7{1'b0}}), .eq(comparator_3_eq));  // open: gt, lt
  Comparator #(.width(7)) comparator_4 (.a(Opcode), .b(7'b0110011), .eq(comparator_4_eq));  // open: gt, lt
  Comparator #(.width(3)) comparator_5 (.a(Funct3), .b(3'b011), .eq(comparator_5_eq));  // open: gt, lt
  Comparator #(.width(7)) comparator_6 (.a(Funct7), .b(7'b0000001), .eq(comparator_6_eq));  // open: gt, lt
  Comparator #(.width(7)) comparator_7 (.a(Opcode), .b(7'b0110011), .eq(comparator_7_eq));  // open: gt, lt
  Comparator #(.width(3)) comparator_8 (.a(Funct3), .b(3'b100), .eq(comparator_8_eq));  // open: gt, lt
  Comparator #(.width(7)) comparator_9 (.a(Funct7), .b({7{1'b0}}), .eq(comparator_9_eq));  // open: gt, lt
  Comparator #(.width(7)) comparator_10 (.a(Opcode), .b(7'b0110011), .eq(comparator_10_eq));  // open: gt, lt
  Comparator #(.width(3)) comparator_11 (.a(Funct3), .b(3'b101), .eq(comparator_11_eq));  // open: gt, lt
  Comparator #(.width(7)) comparator_12 (.a(Funct7), .b(7'b0100000), .eq(comparator_12_eq));  // open: gt, lt
  and u_and_1 (slt, comparator_1_eq, comparator_2_eq, comparator_3_eq);
  and and_2 (mulhu, comparator_4_eq, comparator_5_eq, comparator_6_eq);
  and and_3 (xor_1, comparator_7_eq, comparator_8_eq, comparator_9_eq);
  and and_4 (sra_1, comparator_10_eq, comparator_11_eq, comparator_12_eq);
  Comparator #(.width(7)) comparator_13 (.a(Opcode), .b(7'b0110011), .eq(comparator_13_eq));  // open: gt, lt
  Comparator #(.width(3)) comparator_14 (.a(Funct3), .b(3'b111), .eq(comparator_14_eq));  // open: gt, lt
  Comparator #(.width(7)) comparator_15 (.a(Funct7), .b({7{1'b0}}), .eq(comparator_15_eq));  // open: gt, lt
  Comparator #(.width(7)) comparator_16 (.a(Opcode), .b(7'b0110011), .eq(comparator_16_eq));  // open: gt, lt
  Comparator #(.width(3)) comparator_17 (.a(Funct3), .b(3'b111), .eq(comparator_17_eq));  // open: gt, lt
  Comparator #(.width(7)) comparator_18 (.a(Funct7), .b(7'b0000001), .eq(comparator_18_eq));  // open: gt, lt
  Comparator #(.width(7)) comparator_19 (.a(Opcode), .b(7'b0010011), .eq(comparator_19_eq));  // open: gt, lt
  Comparator #(.width(3)) comparator_20 (.a(Funct3), .b(3'b101), .eq(comparator_20_eq));  // open: gt, lt
  Comparator #(.width(7)) comparator_21 (.a(Funct7), .b(7'b0100000), .eq(comparator_21_eq));  // open: gt, lt
  Comparator #(.width(7)) comparator_22 (.a(Opcode), .b(7'b0110111), .eq(lui));  // open: gt, lt
  Comparator #(.width(7)) comparator_23 (.a(Opcode), .b(7'b1101111), .eq(jal));  // open: gt, lt
  and and_5 (and_1, comparator_13_eq, comparator_14_eq, comparator_15_eq);
  and and_6 (remu, comparator_16_eq, comparator_17_eq, comparator_18_eq);
  and and_7 (srai, comparator_19_eq, comparator_20_eq, comparator_21_eq);
  Comparator #(.width(7)) comparator_24 (.a(Opcode), .b(7'b0010011), .eq(comparator_24_eq));  // open: gt, lt
  Comparator #(.width(3)) comparator_25 (.a(Funct3), .b(3'b010), .eq(comparator_25_eq));  // open: gt, lt
  Comparator #(.width(7)) comparator_26 (.a(Opcode), .b(7'b0010011), .eq(comparator_26_eq));  // open: gt, lt
  Comparator #(.width(3)) comparator_27 (.a(Funct3), .b(3'b100), .eq(comparator_27_eq));  // open: gt, lt
  Comparator #(.width(7)) comparator_28 (.a(Opcode), .b(7'b0010011), .eq(comparator_28_eq));  // open: gt, lt
  Comparator #(.width(3)) comparator_29 (.a(Funct3), .b(3'b111), .eq(comparator_29_eq));  // open: gt, lt
  or or_1 (ALUSel_0, mulhu, xor_1, sra_1, and_1, remu, slt, srai, slti, xori, andi, lui);
  and and_8 (slti, comparator_24_eq, comparator_25_eq);
  and and_9 (xori, comparator_26_eq, comparator_27_eq);
  and and_10 (andi, comparator_28_eq, comparator_29_eq);

  // Other names for the same wires on the sheet: inst[31:0] = Instruction
endmodule

module RegWEn_0 (
  input  [31:0] Instruction,
  output RegWEn
);

  wire beq, blt, bltu, bne, comparator_1_eq, comparator_2_eq, comparator_3_eq, comparator_4_eq,
       comparator_5_eq, comparator_6_eq, comparator_7_eq, comparator_8_eq, comparator_9_eq, comparator_10_eq,
       nothing, or_1_out, sw;
  wire [2:0] Funct3;
  wire [6:0] Funct7, Opcode;

  OpcodeFunctDecoder opcodefunctdecoder_1 (
    .Instruction(Instruction), .Opcode(Opcode), .Funct3(Funct3), .Funct7(Funct7));
  Comparator #(.width(7)) comparator_1 (.a(Opcode), .b(7'b0100011), .eq(comparator_1_eq));  // open: gt, lt
  Comparator #(.width(3)) comparator_2 (.a(Funct3), .b(3'b010), .eq(comparator_2_eq));  // open: gt, lt
  Comparator #(.width(7)) comparator_3 (.a(Opcode), .b(7'b1100011), .eq(comparator_3_eq));  // open: gt, lt
  Comparator #(.width(3)) comparator_4 (.a(Funct3), .b(3'b000), .eq(comparator_4_eq));  // open: gt, lt
  Comparator #(.width(7)) comparator_5 (.a(Opcode), .b(7'b1100011), .eq(comparator_5_eq));  // open: gt, lt
  Comparator #(.width(3)) comparator_6 (.a(Funct3), .b(3'b001), .eq(comparator_6_eq));  // open: gt, lt
  Comparator #(.width(7)) comparator_7 (.a(Opcode), .b(7'b1100011), .eq(comparator_7_eq));  // open: gt, lt
  Comparator #(.width(3)) comparator_8 (.a(Funct3), .b(3'b100), .eq(comparator_8_eq));  // open: gt, lt
  Comparator #(.width(7)) comparator_9 (.a(Opcode), .b(7'b1100011), .eq(comparator_9_eq));  // open: gt, lt
  Comparator #(.width(3)) comparator_10 (.a(Funct3), .b(3'b110), .eq(comparator_10_eq));  // open: gt, lt
  Comparator #(.width(32)) comparator_11 (.a(Instruction), .b({32{1'b0}}), .eq(nothing));  // open: gt, lt
  and and_1 (sw, comparator_1_eq, comparator_2_eq);
  and and_2 (beq, comparator_3_eq, comparator_4_eq);
  and and_3 (bne, comparator_5_eq, comparator_6_eq);
  and and_4 (blt, comparator_7_eq, comparator_8_eq);
  and and_5 (bltu, comparator_9_eq, comparator_10_eq);
  not not_1 (RegWEn, or_1_out);
  or or_1 (or_1_out, bne, sw, beq, blt, bltu, nothing);

  // Other names for the same wires on the sheet: inst[31:0] = Instruction
endmodule

module ImmSel_2 (
  input  [31:0] Instruction,
  output ImmSel_2
);

  wire [2:0] Funct3;
  wire [6:0] Funct7, Opcode;

  OpcodeFunctDecoder opcodefunctdecoder_1 (
    .Instruction(Instruction), .Opcode(Opcode), .Funct3(Funct3), .Funct7(Funct7));
  Comparator #(.width(7)) comparator_1 (.a(Opcode), .b(7'b1101111), .eq(ImmSel_2));  // open: gt, lt

  // Other names for the same wires on the sheet: inst[31:0] = Instruction
endmodule

module ImmSel_1 (
  input  [31:0] Instruction,
  output ImmSel_1
);

  wire beq, blt, bltu, bne, comparator_1_eq, comparator_2_eq, comparator_3_eq, comparator_4_eq,
       comparator_5_eq, comparator_6_eq, comparator_7_eq, comparator_8_eq, lui;
  wire [2:0] Funct3;
  wire [6:0] Funct7, Opcode;

  OpcodeFunctDecoder opcodefunctdecoder_1 (
    .Instruction(Instruction), .Opcode(Opcode), .Funct3(Funct3), .Funct7(Funct7));
  Comparator #(.width(7)) comparator_1 (.a(Opcode), .b(7'b1100011), .eq(comparator_1_eq));  // open: gt, lt
  Comparator #(.width(3)) comparator_2 (.a(Funct3), .b(3'b000), .eq(comparator_2_eq));  // open: gt, lt
  Comparator #(.width(7)) comparator_3 (.a(Opcode), .b(7'b1100011), .eq(comparator_3_eq));  // open: gt, lt
  Comparator #(.width(3)) comparator_4 (.a(Funct3), .b(3'b100), .eq(comparator_4_eq));  // open: gt, lt
  Comparator #(.width(7)) comparator_5 (.a(Opcode), .b(7'b1100011), .eq(comparator_5_eq));  // open: gt, lt
  Comparator #(.width(3)) comparator_6 (.a(Funct3), .b(3'b110), .eq(comparator_6_eq));  // open: gt, lt
  and and_1 (beq, comparator_1_eq, comparator_2_eq);
  and and_2 (blt, comparator_3_eq, comparator_4_eq);
  and and_3 (bltu, comparator_5_eq, comparator_6_eq);
  or or_1 (ImmSel_1, beq, blt, bltu, bne, lui);
  Comparator #(.width(7)) comparator_7 (.a(Opcode), .b(7'b1100011), .eq(comparator_7_eq));  // open: gt, lt
  and and_4 (bne, comparator_7_eq, comparator_8_eq);
  Comparator #(.width(3)) comparator_8 (.a(Funct3), .b(3'b001), .eq(comparator_8_eq));  // open: gt, lt
  Comparator #(.width(7)) comparator_9 (.a(Opcode), .b(7'b0110111), .eq(lui));  // open: gt, lt

  // Other names for the same wires on the sheet: inst[31:0] = Instruction
endmodule

module ImmSel_0 (
  input  [31:0] Instruction,
  output ImmSel_0
);

  wire comparator_1_eq, comparator_2_eq, lui, sw;
  wire [2:0] Funct3;
  wire [6:0] Funct7, Opcode;

  OpcodeFunctDecoder opcodefunctdecoder_1 (
    .Instruction(Instruction), .Opcode(Opcode), .Funct3(Funct3), .Funct7(Funct7));
  Comparator #(.width(7)) comparator_1 (.a(Opcode), .b(7'b0100011), .eq(comparator_1_eq));  // open: gt, lt
  Comparator #(.width(3)) comparator_2 (.a(Funct3), .b(3'b010), .eq(comparator_2_eq));  // open: gt, lt
  Comparator #(.width(7)) comparator_3 (.a(Opcode), .b(7'b0110111), .eq(lui));  // open: gt, lt
  and and_1 (sw, comparator_1_eq, comparator_2_eq);
  or or_1 (ImmSel_0, sw, lui);

  // Other names for the same wires on the sheet: inst[31:0] = Instruction
endmodule

module BrUn_0 (
  input  [31:0] Instruction,
  output BrUn
);

  wire comparator_1_eq, comparator_2_eq;
  wire [2:0] Funct3;
  wire [6:0] Funct7, Opcode;

  OpcodeFunctDecoder opcodefunctdecoder_1 (
    .Instruction(Instruction), .Opcode(Opcode), .Funct3(Funct3), .Funct7(Funct7));
  Comparator #(.width(7)) comparator_1 (.a(Opcode), .b(7'b1100011), .eq(comparator_1_eq));  // open: gt, lt
  Comparator #(.width(3)) comparator_2 (.a(Funct3), .b(3'b110), .eq(comparator_2_eq));  // open: gt, lt
  and and_1 (BrUn, comparator_1_eq, comparator_2_eq);

  // Other names for the same wires on the sheet: inst[31:0] = Instruction
endmodule

module ASel_0 (
  input  [31:0] Instruction,
  output ASel
);

  wire beq, blt, bltu, bne, comparator_1_eq, comparator_2_eq, comparator_3_eq, comparator_4_eq,
       comparator_5_eq, comparator_6_eq, comparator_8_eq, comparator_9_eq, jal;
  wire [2:0] Funct3;
  wire [6:0] Funct7, Opcode;

  OpcodeFunctDecoder opcodefunctdecoder_1 (
    .Instruction(Instruction), .Opcode(Opcode), .Funct3(Funct3), .Funct7(Funct7));
  Comparator #(.width(7)) comparator_1 (.a(Opcode), .b(7'b1100011), .eq(comparator_1_eq));  // open: gt, lt
  Comparator #(.width(3)) comparator_2 (.a(Funct3), .b(3'b000), .eq(comparator_2_eq));  // open: gt, lt
  Comparator #(.width(7)) comparator_3 (.a(Opcode), .b(7'b1100011), .eq(comparator_3_eq));  // open: gt, lt
  Comparator #(.width(3)) comparator_4 (.a(Funct3), .b(3'b100), .eq(comparator_4_eq));  // open: gt, lt
  Comparator #(.width(7)) comparator_5 (.a(Opcode), .b(7'b1100011), .eq(comparator_5_eq));  // open: gt, lt
  Comparator #(.width(3)) comparator_6 (.a(Funct3), .b(3'b110), .eq(comparator_6_eq));  // open: gt, lt
  Comparator #(.width(7)) comparator_7 (.a(Opcode), .b(7'b1101111), .eq(jal));  // open: gt, lt
  and and_1 (beq, comparator_1_eq, comparator_2_eq);
  and and_2 (blt, comparator_3_eq, comparator_4_eq);
  and and_3 (bltu, comparator_5_eq, comparator_6_eq);
  or or_1 (ASel, beq, blt, jal, bltu, bne);
  Comparator #(.width(7)) comparator_8 (.a(Opcode), .b(7'b1100011), .eq(comparator_8_eq));  // open: gt, lt
  and and_4 (bne, comparator_8_eq, comparator_9_eq);
  Comparator #(.width(3)) comparator_9 (.a(Funct3), .b(3'b001), .eq(comparator_9_eq));  // open: gt, lt

  // Other names for the same wires on the sheet: inst[31:0] = Instruction
endmodule

module BSel_0 (
  input  [31:0] Instruction,
  output BSel
);

  wire add, and_1, comparator_1_eq, comparator_2_eq, comparator_3_eq, comparator_4_eq, comparator_5_eq,
       comparator_6_eq, comparator_7_eq, comparator_8_eq, comparator_9_eq, comparator_10_eq,
       comparator_11_eq, comparator_12_eq, comparator_13_eq, comparator_14_eq, comparator_15_eq,
       comparator_16_eq, comparator_17_eq, comparator_18_eq, comparator_19_eq, comparator_20_eq,
       comparator_21_eq, comparator_22_eq, comparator_23_eq, comparator_24_eq, comparator_25_eq,
       comparator_26_eq, comparator_27_eq, comparator_28_eq, comparator_29_eq, comparator_30_eq,
       comparator_31_eq, comparator_32_eq, comparator_33_eq, comparator_34_eq, comparator_35_eq,
       comparator_36_eq, comparator_37_eq, comparator_38_eq, comparator_39_eq, comparator_40_eq,
       comparator_41_eq, comparator_42_eq, divu, mul, mulh, mulhu, or_1, or_1_out, remu, sll_1, slt, sra_1,
       srl_1, sub, xor_1;
  wire [2:0] Funct3;
  wire [6:0] Funct7, Opcode;

  OpcodeFunctDecoder opcodefunctdecoder_1 (
    .Instruction(Instruction), .Opcode(Opcode), .Funct3(Funct3), .Funct7(Funct7));
  Comparator #(.width(7)) comparator_1 (.a(Opcode), .b(7'b0110011), .eq(comparator_1_eq));  // open: gt, lt
  Comparator #(.width(3)) comparator_2 (.a(Funct3), .b(3'b000), .eq(comparator_2_eq));  // open: gt, lt
  Comparator #(.width(7)) comparator_3 (.a(Funct7), .b({7{1'b0}}), .eq(comparator_3_eq));  // open: gt, lt
  Comparator #(.width(7)) comparator_4 (.a(Opcode), .b(7'b0110011), .eq(comparator_4_eq));  // open: gt, lt
  Comparator #(.width(3)) comparator_5 (.a(Funct3), .b(3'b000), .eq(comparator_5_eq));  // open: gt, lt
  Comparator #(.width(7)) comparator_6 (.a(Funct7), .b(7'b0000001), .eq(comparator_6_eq));  // open: gt, lt
  Comparator #(.width(7)) comparator_7 (.a(Opcode), .b(7'b0110011), .eq(comparator_7_eq));  // open: gt, lt
  Comparator #(.width(3)) comparator_8 (.a(Funct3), .b(3'b000), .eq(comparator_8_eq));  // open: gt, lt
  Comparator #(.width(7)) comparator_9 (.a(Funct7), .b(7'b0100000), .eq(comparator_9_eq));  // open: gt, lt
  Comparator #(.width(7)) comparator_10 (.a(Opcode), .b(7'b0110011), .eq(comparator_10_eq));  // open: gt, lt
  Comparator #(.width(3)) comparator_11 (.a(Funct3), .b(3'b001), .eq(comparator_11_eq));  // open: gt, lt
  Comparator #(.width(7)) comparator_12 (.a(Funct7), .b({7{1'b0}}), .eq(comparator_12_eq));  // open: gt, lt
  Comparator #(.width(7)) comparator_13 (.a(Opcode), .b(7'b0110011), .eq(comparator_13_eq));  // open: gt, lt
  Comparator #(.width(3)) comparator_14 (.a(Funct3), .b(3'b001), .eq(comparator_14_eq));  // open: gt, lt
  Comparator #(.width(7)) comparator_15 (.a(Funct7), .b(7'b0000001), .eq(comparator_15_eq));  // open: gt, lt
  and u_and_1 (add, comparator_1_eq, comparator_2_eq, comparator_3_eq);
  and and_2 (mul, comparator_4_eq, comparator_5_eq, comparator_6_eq);
  and and_3 (sub, comparator_7_eq, comparator_8_eq, comparator_9_eq);
  and and_4 (sll_1, comparator_10_eq, comparator_11_eq, comparator_12_eq);
  and and_5 (mulh, comparator_13_eq, comparator_14_eq, comparator_15_eq);
  Comparator #(.width(7)) comparator_16 (.a(Opcode), .b(7'b0110011), .eq(comparator_16_eq));  // open: gt, lt
  Comparator #(.width(3)) comparator_17 (.a(Funct3), .b(3'b010), .eq(comparator_17_eq));  // open: gt, lt
  Comparator #(.width(7)) comparator_18 (.a(Funct7), .b({7{1'b0}}), .eq(comparator_18_eq));  // open: gt, lt
  Comparator #(.width(7)) comparator_19 (.a(Opcode), .b(7'b0110011), .eq(comparator_19_eq));  // open: gt, lt
  Comparator #(.width(3)) comparator_20 (.a(Funct3), .b(3'b011), .eq(comparator_20_eq));  // open: gt, lt
  Comparator #(.width(7)) comparator_21 (.a(Funct7), .b(7'b0000001), .eq(comparator_21_eq));  // open: gt, lt
  Comparator #(.width(7)) comparator_22 (.a(Opcode), .b(7'b0110011), .eq(comparator_22_eq));  // open: gt, lt
  Comparator #(.width(3)) comparator_23 (.a(Funct3), .b(3'b100), .eq(comparator_23_eq));  // open: gt, lt
  Comparator #(.width(7)) comparator_24 (.a(Funct7), .b({7{1'b0}}), .eq(comparator_24_eq));  // open: gt, lt
  Comparator #(.width(7)) comparator_25 (.a(Opcode), .b(7'b0110011), .eq(comparator_25_eq));  // open: gt, lt
  Comparator #(.width(3)) comparator_26 (.a(Funct3), .b(3'b101), .eq(comparator_26_eq));  // open: gt, lt
  Comparator #(.width(7)) comparator_27 (.a(Funct7), .b({7{1'b0}}), .eq(comparator_27_eq));  // open: gt, lt
  Comparator #(.width(7)) comparator_28 (.a(Opcode), .b(7'b0110011), .eq(comparator_28_eq));  // open: gt, lt
  Comparator #(.width(3)) comparator_29 (.a(Funct3), .b(3'b101), .eq(comparator_29_eq));  // open: gt, lt
  Comparator #(.width(7)) comparator_30 (.a(Funct7), .b(7'b0100000), .eq(comparator_30_eq));  // open: gt, lt
  and and_6 (slt, comparator_16_eq, comparator_17_eq, comparator_18_eq);
  and and_7 (mulhu, comparator_19_eq, comparator_20_eq, comparator_21_eq);
  and and_8 (xor_1, comparator_22_eq, comparator_23_eq, comparator_24_eq);
  and and_9 (srl_1, comparator_25_eq, comparator_26_eq, comparator_27_eq);
  and and_10 (sra_1, comparator_28_eq, comparator_29_eq, comparator_30_eq);
  Comparator #(.width(7)) comparator_31 (.a(Opcode), .b(7'b0110011), .eq(comparator_31_eq));  // open: gt, lt
  Comparator #(.width(3)) comparator_32 (.a(Funct3), .b(3'b101), .eq(comparator_32_eq));  // open: gt, lt
  Comparator #(.width(7)) comparator_33 (.a(Funct7), .b(7'b0000001), .eq(comparator_33_eq));  // open: gt, lt
  Comparator #(.width(7)) comparator_34 (.a(Opcode), .b(7'b0110011), .eq(comparator_34_eq));  // open: gt, lt
  Comparator #(.width(3)) comparator_35 (.a(Funct3), .b(3'b110), .eq(comparator_35_eq));  // open: gt, lt
  Comparator #(.width(7)) comparator_36 (.a(Funct7), .b({7{1'b0}}), .eq(comparator_36_eq));  // open: gt, lt
  Comparator #(.width(7)) comparator_37 (.a(Opcode), .b(7'b0110011), .eq(comparator_37_eq));  // open: gt, lt
  Comparator #(.width(3)) comparator_38 (.a(Funct3), .b(3'b111), .eq(comparator_38_eq));  // open: gt, lt
  Comparator #(.width(7)) comparator_39 (.a(Funct7), .b({7{1'b0}}), .eq(comparator_39_eq));  // open: gt, lt
  Comparator #(.width(7)) comparator_40 (.a(Opcode), .b(7'b0110011), .eq(comparator_40_eq));  // open: gt, lt
  Comparator #(.width(3)) comparator_41 (.a(Funct3), .b(3'b111), .eq(comparator_41_eq));  // open: gt, lt
  Comparator #(.width(7)) comparator_42 (.a(Funct7), .b(7'b0000001), .eq(comparator_42_eq));  // open: gt, lt
  or u_or_1 (or_1_out, add, mul, sub, sll_1, mulh, slt, mulhu, xor_1, srl_1, sra_1, divu, or_1, and_1, remu);
  and and_11 (divu, comparator_31_eq, comparator_32_eq, comparator_33_eq);
  and and_12 (or_1, comparator_34_eq, comparator_35_eq, comparator_36_eq);
  and and_13 (and_1, comparator_37_eq, comparator_38_eq, comparator_39_eq);
  and and_14 (remu, comparator_40_eq, comparator_41_eq, comparator_42_eq);
  not not_1 (BSel, or_1_out);

  // Other names for the same wires on the sheet: inst[31:0] = Instruction
endmodule

module MemRW_0 (
  input  [31:0] Instruction,
  output MemRW
);

  wire comparator_1_eq, comparator_2_eq;
  wire [2:0] Funct3;
  wire [6:0] Funct7, Opcode;

  OpcodeFunctDecoder opcodefunctdecoder_1 (
    .Instruction(Instruction), .Opcode(Opcode), .Funct3(Funct3), .Funct7(Funct7));
  Comparator #(.width(7)) comparator_1 (.a(Opcode), .b(7'b0100011), .eq(comparator_1_eq));  // open: gt, lt
  Comparator #(.width(3)) comparator_2 (.a(Funct3), .b(3'b010), .eq(comparator_2_eq));  // open: gt, lt
  and and_1 (MemRW, comparator_1_eq, comparator_2_eq);

  // Other names for the same wires on the sheet: inst[31:0] = Instruction
endmodule

module WBSel_1 (
  input  [31:0] Instruction,
  output WBSel_1
);

  wire comparator_1_eq, comparator_2_eq, comparator_3_eq, comparator_4_eq, comparator_5_eq, comparator_6_eq,
       lb, lh, lw;
  wire [2:0] Funct3;
  wire [6:0] Funct7, Opcode;

  OpcodeFunctDecoder opcodefunctdecoder_1 (
    .Instruction(Instruction), .Opcode(Opcode), .Funct3(Funct3), .Funct7(Funct7));
  Comparator #(.width(7)) comparator_1 (.a(Opcode), .b(7'b0000011), .eq(comparator_1_eq));  // open: gt, lt
  Comparator #(.width(3)) comparator_2 (.a(Funct3), .b(3'b000), .eq(comparator_2_eq));  // open: gt, lt
  Comparator #(.width(7)) comparator_3 (.a(Opcode), .b(7'b0000011), .eq(comparator_3_eq));  // open: gt, lt
  Comparator #(.width(3)) comparator_4 (.a(Funct3), .b(3'b001), .eq(comparator_4_eq));  // open: gt, lt
  Comparator #(.width(7)) comparator_5 (.a(Opcode), .b(7'b0000011), .eq(comparator_5_eq));  // open: gt, lt
  Comparator #(.width(3)) comparator_6 (.a(Funct3), .b(3'b010), .eq(comparator_6_eq));  // open: gt, lt
  and and_1 (lb, comparator_1_eq, comparator_2_eq);
  and and_2 (lh, comparator_3_eq, comparator_4_eq);
  and and_3 (lw, comparator_5_eq, comparator_6_eq);
  or or_1 (WBSel_1, lb, lh, lw);

  // Other names for the same wires on the sheet: inst[31:0] = Instruction
endmodule

module WBSel_0 (
  input  [31:0] Instruction,
  output WBSel_0
);

  wire comparator_1_eq, comparator_2_eq, comparator_3_eq, comparator_4_eq, comparator_5_eq, comparator_6_eq,
       comparator_7_eq, comparator_8_eq, jal, jalr, lb, lh, lw, or_1_out;
  wire [2:0] Funct3;
  wire [6:0] Funct7, Opcode;

  OpcodeFunctDecoder opcodefunctdecoder_1 (
    .Instruction(Instruction), .Opcode(Opcode), .Funct3(Funct3), .Funct7(Funct7));
  Comparator #(.width(7)) comparator_1 (.a(Opcode), .b(7'b0000011), .eq(comparator_1_eq));  // open: gt, lt
  and and_1 (lb, comparator_1_eq, comparator_2_eq);
  Comparator #(.width(3)) comparator_2 (.a(Funct3), .b(3'b000), .eq(comparator_2_eq));  // open: gt, lt
  Comparator #(.width(7)) comparator_3 (.a(Opcode), .b(7'b0000011), .eq(comparator_3_eq));  // open: gt, lt
  and and_2 (lh, comparator_3_eq, comparator_4_eq);
  Comparator #(.width(3)) comparator_4 (.a(Funct3), .b(3'b001), .eq(comparator_4_eq));  // open: gt, lt
  Comparator #(.width(7)) comparator_5 (.a(Opcode), .b(7'b0000011), .eq(comparator_5_eq));  // open: gt, lt
  and and_3 (lw, comparator_5_eq, comparator_6_eq);
  Comparator #(.width(3)) comparator_6 (.a(Funct3), .b(3'b010), .eq(comparator_6_eq));  // open: gt, lt
  Comparator #(.width(7)) comparator_7 (.a(Opcode), .b(7'b1100111), .eq(comparator_7_eq));  // open: gt, lt
  Comparator #(.width(3)) comparator_8 (.a(Funct3), .b(3'b000), .eq(comparator_8_eq));  // open: gt, lt
  Comparator #(.width(7)) comparator_9 (.a(Opcode), .b(7'b1101111), .eq(jal));  // open: gt, lt
  or or_1 (or_1_out, lb, lh, lw, jalr, jal);
  not not_1 (WBSel_0, or_1_out);
  and and_4 (jalr, comparator_7_eq, comparator_8_eq);

  // Other names for the same wires on the sheet: inst[31:0] = Instruction
endmodule

module PCSel_0 (
  input  [31:0] Instruction,
  input  BrEq,
  input  BrLt,
  output PCSel
);

  wire beq, blt, bltu, bne, comparator_1_eq, comparator_2_eq, comparator_3_eq, comparator_4_eq,
       comparator_5_eq, comparator_6_eq, comparator_7_eq, comparator_8_eq, comparator_10_eq,
       comparator_11_eq, jal, jalr;
  wire [2:0] Funct3;
  wire [6:0] Funct7, Opcode;

  OpcodeFunctDecoder opcodefunctdecoder_1 (
    .Instruction(Instruction), .Opcode(Opcode), .Funct3(Funct3), .Funct7(Funct7));
  Comparator #(.width(7)) comparator_1 (.a(Opcode), .b(7'b1100111), .eq(comparator_1_eq));  // open: gt, lt
  and and_1 (jalr, comparator_1_eq, comparator_2_eq);
  Comparator #(.width(3)) comparator_2 (.a(Funct3), .b(3'b000), .eq(comparator_2_eq));  // open: gt, lt
  Comparator #(.width(7)) comparator_3 (.a(Opcode), .b(7'b1100011), .eq(comparator_3_eq));  // open: gt, lt
  and and_2 (beq, comparator_3_eq, comparator_4_eq, BrEq);
  Comparator #(.width(3)) comparator_4 (.a(Funct3), .b(3'b000), .eq(comparator_4_eq));  // open: gt, lt
  Comparator #(.width(7)) comparator_5 (.a(Opcode), .b(7'b1100011), .eq(comparator_5_eq));  // open: gt, lt
  and and_3 (blt, comparator_5_eq, comparator_6_eq, BrLt);
  Comparator #(.width(3)) comparator_6 (.a(Funct3), .b(3'b100), .eq(comparator_6_eq));  // open: gt, lt
  Comparator #(.width(7)) comparator_7 (.a(Opcode), .b(7'b1100011), .eq(comparator_7_eq));  // open: gt, lt
  Comparator #(.width(3)) comparator_8 (.a(Funct3), .b(3'b110), .eq(comparator_8_eq));  // open: gt, lt
  and and_4 (bltu, comparator_7_eq, comparator_8_eq, BrLt);
  Comparator #(.width(7)) comparator_9 (.a(Opcode), .b(7'b1101111), .eq(jal));  // open: gt, lt
  Comparator #(.width(7)) comparator_10 (.a(Opcode), .b(7'b1100011), .eq(comparator_10_eq));  // open: gt, lt
  Comparator #(.width(3)) comparator_11 (.a(Funct3), .b(3'b001), .eq(comparator_11_eq));  // open: gt, lt
  and and_5 (bne, comparator_10_eq, comparator_11_eq, ~BrEq);  // AND_Gate
  or or_1 (PCSel, jalr, beq, blt, bltu, bne, jal);

  // Other names for the same wires on the sheet: inst[31:0] = Instruction
endmodule

module LoadSel_1 (
  input  [31:0] Instruction,
  output LoadSel_1
);

  wire comparator_1_eq, comparator_2_eq;
  wire [2:0] Funct3;
  wire [6:0] Funct7, Opcode;

  OpcodeFunctDecoder opcodefunctdecoder_1 (
    .Instruction(Instruction), .Opcode(Opcode), .Funct3(Funct3), .Funct7(Funct7));
  Comparator #(.width(7)) comparator_1 (.a(Opcode), .b(7'b0000011), .eq(comparator_1_eq));  // open: gt, lt
  Comparator #(.width(3)) comparator_2 (.a(Funct3), .b(3'b010), .eq(comparator_2_eq));  // open: gt, lt
  and and_1 (LoadSel_1, comparator_1_eq, comparator_2_eq);

  // Other names for the same wires on the sheet: inst[31:0] = Instruction
endmodule

module LoadSel_0 (
  input  [31:0] Instruction,
  output LoadSel_0
);

  wire comparator_1_eq, comparator_2_eq;
  wire [2:0] Funct3;
  wire [6:0] Funct7, Opcode;

  OpcodeFunctDecoder opcodefunctdecoder_1 (
    .Instruction(Instruction), .Opcode(Opcode), .Funct3(Funct3), .Funct7(Funct7));
  Comparator #(.width(7)) comparator_1 (.a(Opcode), .b(7'b0000011), .eq(comparator_1_eq));  // open: gt, lt
  Comparator #(.width(3)) comparator_2 (.a(Funct3), .b(3'b001), .eq(comparator_2_eq));  // open: gt, lt
  and and_1 (LoadSel_0, comparator_1_eq, comparator_2_eq);

  // Other names for the same wires on the sheet: inst[31:0] = Instruction
endmodule
