// Logisim project CPU-TEST_UNIT_bne.circ as structural Verilog: 1 circuit, main circuit main
module main (
  output [31:0] ra,
  output [31:0] sp,
  output [31:0] t0,
  output [31:0] t1,
  output [31:0] t2,
  output [31:0] s0,
  output [31:0] s1,
  output [31:0] a0,
  output [31:0] Requested_Address,
  output [31:0] Requested_Instruction,
  output [15:0] Time_Step,
  output halt
);

  wire clk;

  Clock clock_1 (.out(clk));
  // Probe on Requested_Address
  ROM #(.addrWidth(14), .dataWidth(32)) rom_1 (.addr(Requested_Address[15:2]), .data(Requested_Instruction));
  cpu_main main_1 (
    .INSTRUCTION(Requested_Instruction), .CLOCK(clk), .ra(ra), .sp(sp), .t0(t0), .t1(t1), .t2(t2), .s0(s0),
    .s1(s1), .a0(a0), .PROGRAM_COUNTER(Requested_Address));
  // Probe on Requested_Instruction
  Counter #(.width(16), .max('hffff)) counter_1 (.clk(clk), .Q(Time_Step));  // open: clr, load, up, count, D, carry
  Comparator #(.width(16)) comparator_1 (.a(Time_Step), .b(16'h4e), .eq(halt));  // open: gt, lt

  // Other names for the same wires on the sheet: fetch_addr[31:0] = Requested_Address;
  //   Instruction[31:0] = Requested_Instruction

  // Notes on the sheet:
  //   contents of rom_1 (hex, n*v repeats v):
  //   00001463 00000033 00000033 00100513 00200413 00851863 00000033 00000033 00000033 00000033 00200513
  //   00100413 00851A63 00000033 00000033 00000033 00000033 00000033 00400513 00400413 00851A63 00000033
  //   00000033 00000033 00000033 00000033 00000033 00000033 FFF00513 FFE00413 00851863 00000033 00000033
  //   00000033 00000033 FFE00513 FFF00413 00851A63 00000033 00000033 00000033 00000033 00000033 FFC00513
  //   FFC00413 00851A63 00000033 00000033 00000033 00000033 00000033 00000033 FF600113 00110113 FE011EE3
  //   00A00113 00500493 FFF10113 FE914EE3 00000533
  //   YOUR CPU SHOULD FIT IN HERE!
  //   Instruction Memory
  //   Halts Execution After Constant # of Clock Cycles
  //   Constant
endmodule
