// Logisim project CPU-TEST_UNIT_divu.circ as structural Verilog: 1 circuit, main circuit main
module main (
  output [31:0] ra,
  output [31:0] sp,
  output [31:0] t0,
  output [31:0] t1,
  output [31:0] t2,
  output [31:0] s0,
  output [31:0] s1,
  output [31:0] a0,
  output [31:0] Requested_Address,
  output [31:0] Requested_Instruction,
  output [15:0] Time_Step,
  output halt
);

  wire clk;

  Clock clock_1 (.out(clk));
  // Probe on Requested_Address
  ROM #(.addrWidth(14), .dataWidth(32)) rom_1 (.addr(Requested_Address[15:2]), .data(Requested_Instruction));
  cpu_main main_1 (
    .INSTRUCTION(Requested_Instruction), .CLOCK(clk), .ra(ra), .sp(sp), .t0(t0), .t1(t1), .t2(t2), .s0(s0),
    .s1(s1), .a0(a0), .PROGRAM_COUNTER(Requested_Address));
  // Probe on Requested_Instruction
  Counter #(.width(16), .max('hffff)) counter_1 (.clk(clk), .Q(Time_Step));  // open: clr, load, up, count, D, carry
  Comparator #(.width(16)) comparator_1 (.a(Time_Step), .b(16'h44), .eq(halt));  // open: gt, lt

  // Other names for the same wires on the sheet: fetch_addr[31:0] = Requested_Address;
  //   Instruction[31:0] = Requested_Instruction

  // Notes on the sheet:
  //   contents of rom_1 (hex, n*v repeats v):
  //   01800413 00600493 00400293 FFE00313 00700393 029450B3 025450B3 0284D0B3 0282D0B3 028050B3 028450B3
  //   0262D133 02535133 02635133 0253D133 02735133 00200413 00700493 029450B3 0284D0B3 0294D0B3 FFE00293
  //   FF900313 0252D133 0262D133 02535133 02635133 02645133 0292D133 0264D133 02935133 00200413 02000493
  //   FFE00513 02A450B3 00100513 02A450B3 00200513 02A450B3 00300513 02A450B3 00C00513 02A450B3 01100513
  //   02A450B3 01300513 02A450B3 08400513 02A450B3 00400513 02A4D133 02100513 02A4D133 FDF00513 02A4D133
  //   F8000513 02A4D133 FFF00513 02A4D133 FE000513 00A002B3 00000513 02A2D333 00500513 02A2D333 FDF00513
  //   02A2D333
  //   YOUR CPU SHOULD FIT IN HERE!
  //   Instruction Memory
  //   Halts Execution After Constant # of Clock Cycles
  //   Constant
endmodule
