// Logisim project CPU-TEST_UNIT_remu.circ as structural Verilog: 1 circuit, main circuit main
module main (
  output [31:0] ra,
  output [31:0] sp,
  output [31:0] t0,
  output [31:0] t1,
  output [31:0] t2,
  output [31:0] s0,
  output [31:0] s1,
  output [31:0] a0,
  output [31:0] Requested_Address,
  output [31:0] Requested_Instruction,
  output [15:0] Time_Step,
  output halt
);

  wire clk;

  Clock clock_1 (.out(clk));
  // Probe on Requested_Address
  ROM #(.addrWidth(14), .dataWidth(32)) rom_1 (.addr(Requested_Address[15:2]), .data(Requested_Instruction));
  cpu_main main_1 (
    .INSTRUCTION(Requested_Instruction), .CLOCK(clk), .ra(ra), .sp(sp), .t0(t0), .t1(t1), .t2(t2), .s0(s0),
    .s1(s1), .a0(a0), .PROGRAM_COUNTER(Requested_Address));
  // Probe on Requested_Instruction
  Counter #(.width(16), .max('hffff)) counter_1 (.clk(clk), .Q(Time_Step));  // open: clr, load, up, count, D, carry
  Comparator #(.width(16)) comparator_1 (.a(Time_Step), .b(16'h36), .eq(halt));  // open: gt, lt

  // Other names for the same wires on the sheet: fetch_addr[31:0] = Requested_Address;
  //   Instruction[31:0] = Requested_Instruction

  // Notes on the sheet:
  //   contents of rom_1 (hex, n*v repeats v):
  //   00200413 00700493 029470B3 0284F0B3 0294F0B3 FFE00293 FF900313 0252F133 0262F133 02537133 02637133
  //   02647133 0292F133 0264F133 02937133 00200413 02000493 00000513 02A470B3 00100513 02A470B3 00200513
  //   02A470B3 00300513 02A470B3 00C00513 02A470B3 01100513 02A470B3 01300513 02A470B3 08400513 02A470B3
  //   00400513 02A4F133 00000513 02A4F133 02100513 02A4F133 FDF00513 02A4F133 F8000513 02A4F133 FFF00513
  //   02A4F133 FE000513 00A002B3 00000513 02A2F333 00500513 02A2F333 FDF00513 02A2F333
  //   YOUR CPU SHOULD FIT IN HERE!
  //   Instruction Memory
  //   Halts Execution After Constant # of Clock Cycles
  //   Constant
endmodule
