// Logisim project CPU-TEST_UNIT_slli.circ as structural Verilog: 1 circuit, main circuit main
module main (
  output [31:0] ra,
  output [31:0] sp,
  output [31:0] t0,
  output [31:0] t1,
  output [31:0] t2,
  output [31:0] s0,
  output [31:0] s1,
  output [31:0] a0,
  output [31:0] Requested_Address,
  output [31:0] Requested_Instruction,
  output [15:0] Time_Step,
  output halt
);

  wire clk;

  Clock clock_1 (.out(clk));
  // Probe on Requested_Address
  ROM #(.addrWidth(14), .dataWidth(32)) rom_1 (.addr(Requested_Address[15:2]), .data(Requested_Instruction));
  cpu_main main_1 (
    .INSTRUCTION(Requested_Instruction), .CLOCK(clk), .ra(ra), .sp(sp), .t0(t0), .t1(t1), .t2(t2), .s0(s0),
    .s1(s1), .a0(a0), .PROGRAM_COUNTER(Requested_Address));
  // Probe on Requested_Instruction
  Counter #(.width(16), .max('hffff)) counter_1 (.clk(clk), .Q(Time_Step));  // open: clr, load, up, count, D, carry
  Comparator #(.width(16)) comparator_1 (.a(Time_Step), .b(16'hbe), .eq(halt));  // open: gt, lt

  // Other names for the same wires on the sheet: fetch_addr[31:0] = Requested_Address;
  //   Instruction[31:0] = Requested_Instruction

  // Notes on the sheet:
  //   contents of rom_1 (hex, n*v repeats v):
  //   00200413 00700493 00249093 00741113 00041293 00241093 00100313 00031313 00131313 00231313 00331313
  //   00431313 00531313 00631313 00731313 00831313 00931313 00A31313 00B31313 00C31313 00D31313 00E31313
  //   00F31313 01031313 00100393 01F39393 FE000293 00229293 00029293 123452B7 67828293 00029293 123452B7
  //   67828293 00129293 123452B7 67828293 00229293 123452B7 67828293 00329293 123452B7 67828293 00429293
  //   123452B7 67828293 00529293 123452B7 67828293 00629293 123452B7 67828293 00729293 123452B7 67828293
  //   00829293 123452B7 67828293 00929293 123452B7 67828293 00A29293 123452B7 67828293 00B29293 123452B7
  //   67828293 00C29293 123452B7 67828293 00D29293 123452B7 67828293 00E29293 123452B7 67828293 00F29293
  //   123452B7 67828293 01029293 123452B7 67828293 01129293 123452B7 67828293 01229293 123452B7 67828293
  //   01329293 123452B7 67828293 01429293 123452B7 67828293 01529293 123452B7 67828293 01629293 123452B7
  //   67828293 01729293 123452B7 67828293 01829293 123452B7 67828293 01929293 123452B7 67828293 01A29293
  //   123452B7 67828293 01B29293 123452B7 67828293 01C29293 123452B7 67828293 01D29293 123452B7 67828293
  //   01E29293 123452B7 67828293 01F29293 FFF28293 00029293 FFF28293 00129293 FFF28293 00229293 FFF28293
  //   00329293 FFF28293 00429293 FFF28293 00529293 FFF28293 00629293 FFF28293 00729293 FFF28293 00829293
  //   FFF28293 00929293 FFF28293 00A29293 FFF28293 00B29293 FFF28293 00C29293 FFF28293 00D29293 FFF28293
  //   00E29293 FFF28293 00F29293 FFF28293 01029293 FFF28293 01129293 FFF28293 01229293 FFF28293 01329293
  //   FFF28293 01429293 FFF28293 01529293 FFF28293 01629293 FFF28293 01729293 FFF28293 01829293 FFF28293
  //   01929293 FFF28293 01A29293 FFF28293 01B29293 FFF28293 01C29293 FFF28293 01D29293 FFF28293 01E29293
  //   FFF28293 01F29293
  //   YOUR CPU SHOULD FIT IN HERE!
  //   Instruction Memory
  //   Halts Execution After Constant # of Clock Cycles
  //   Constant
endmodule
