// Logisim project CPU-TEST_UNIT_srai.circ as structural Verilog: 1 circuit, main circuit main
module main (
  output [31:0] ra,
  output [31:0] sp,
  output [31:0] t0,
  output [31:0] t1,
  output [31:0] t2,
  output [31:0] s0,
  output [31:0] s1,
  output [31:0] a0,
  output [31:0] Requested_Address,
  output [31:0] Requested_Instruction,
  output [15:0] Time_Step,
  output halt
);

  wire clk;

  Clock clock_1 (.out(clk));
  // Probe on Requested_Address
  ROM #(.addrWidth(14), .dataWidth(32)) rom_1 (.addr(Requested_Address[15:2]), .data(Requested_Instruction));
  cpu_main main_1 (
    .INSTRUCTION(Requested_Instruction), .CLOCK(clk), .ra(ra), .sp(sp), .t0(t0), .t1(t1), .t2(t2), .s0(s0),
    .s1(s1), .a0(a0), .PROGRAM_COUNTER(Requested_Address));
  // Probe on Requested_Instruction
  Counter #(.width(16), .max('hffff)) counter_1 (.clk(clk), .Q(Time_Step));  // open: clr, load, up, count, D, carry
  Comparator #(.width(16)) comparator_1 (.a(Time_Step), .b(16'hbe), .eq(halt));  // open: gt, lt

  // Other names for the same wires on the sheet: fetch_addr[31:0] = Requested_Address;
  //   Instruction[31:0] = Requested_Instruction

  // Notes on the sheet:
  //   contents of rom_1 (hex, n*v repeats v):
  //   00200413 08000493 4024D093 40745113 40045293 40245093 08000313 40035313 40135313 40235313 40335313
  //   40435313 40535313 40635313 40735313 40835313 40935313 40A35313 40B35313 40C35313 40D35313 40E35313
  //   40F35313 41035313 08000393 41F3D393 F8000293 4022D293 4002D293 123452B7 67828293 4002D293 123452B7
  //   67828293 4012D293 123452B7 67828293 4022D293 123452B7 67828293 4032D293 123452B7 67828293 4042D293
  //   123452B7 67828293 4052D293 123452B7 67828293 4062D293 123452B7 67828293 4072D293 123452B7 67828293
  //   4082D293 123452B7 67828293 4092D293 123452B7 67828293 40A2D293 123452B7 67828293 40B2D293 123452B7
  //   67828293 40C2D293 123452B7 67828293 40D2D293 123452B7 67828293 40E2D293 123452B7 67828293 40F2D293
  //   123452B7 67828293 4102D293 123452B7 67828293 4112D293 123452B7 67828293 4122D293 123452B7 67828293
  //   4132D293 123452B7 67828293 4142D293 123452B7 67828293 4152D293 123452B7 67828293 4162D293 123452B7
  //   67828293 4172D293 123452B7 67828293 4182D293 123452B7 67828293 4192D293 123452B7 67828293 41A2D293
  //   123452B7 67828293 41B2D293 123452B7 67828293 41C2D293 123452B7 67828293 41D2D293 123452B7 67828293
  //   41E2D293 123452B7 67828293 41F2D293 FFF28293 4002D293 FFF28293 4012D293 FFF28293 4022D293 FFF28293
  //   4032D293 FFF28293 4042D293 FFF28293 4052D293 FFF28293 4062D293 FFF28293 4072D293 FFF28293 4082D293
  //   FFF28293 4092D293 FFF28293 40A2D293 FFF28293 40B2D293 FFF28293 40C2D293 FFF28293 40D2D293 FFF28293
  //   40E2D293 FFF28293 40F2D293 FFF28293 4102D293 FFF28293 4112D293 FFF28293 4122D293 FFF28293 4132D293
  //   FFF28293 4142D293 FFF28293 4152D293 FFF28293 4162D293 FFF28293 4172D293 FFF28293 4182D293 FFF28293
  //   4192D293 FFF28293 41A2D293 FFF28293 41B2D293 FFF28293 41C2D293 FFF28293 41D2D293 FFF28293 41E2D293
  //   FFF28293 41F2D293
  //   YOUR CPU SHOULD FIT IN HERE!
  //   Instruction Memory
  //   Halts Execution After Constant # of Clock Cycles
  //   Constant
endmodule
