// Logisim project CPU-asdf.circ as structural Verilog: 1 circuit, main circuit main
module main (
  output [31:0] ra,
  output [31:0] sp,
  output [31:0] t0,
  output [31:0] t1,
  output [31:0] t2,
  output [31:0] s0,
  output [31:0] s1,
  output [31:0] a0,
  output [31:0] Requested_Address,
  output [31:0] Requested_Instruction,
  output [15:0] Time_Step,
  output halt
);

  wire clk;

  Clock clock_1 (.out(clk));
  // Probe on Requested_Address
  ROM #(.addrWidth(14), .dataWidth(32)) rom_1 (.addr(Requested_Address[15:2]), .data(Requested_Instruction));
  cpu_main main_1 (
    .INSTRUCTION(Requested_Instruction), .CLOCK(clk), .ra(ra), .sp(sp), .t0(t0), .t1(t1), .t2(t2), .s0(s0),
    .s1(s1), .a0(a0), .PROGRAM_COUNTER(Requested_Address));
  // Probe on Requested_Instruction
  Counter #(.width(16), .max('hffff)) counter_1 (.clk(clk), .Q(Time_Step));  // open: clr, load, up, count, D, carry
  Comparator #(.width(16)) comparator_1 (.a(Time_Step), .b(16'h60), .eq(halt));  // open: gt, lt

  // Other names for the same wires on the sheet: fetch_addr[31:0] = Requested_Address;
  //   Instruction[31:0] = Requested_Instruction

  // Notes on the sheet:
  //   contents of rom_1 (hex, n*v repeats v):
  //   FFF00293 001C82B7 00300293 00700313 00431393 00031393 FFD2A393 00032393 0032A393 00134393 00134393
  //   00034393 00034393 FFF34393 FFF34393 00535393 00035393 40535393 40035393 00136393 00136393 00036393
  //   00036393 FFF36393 FFF36393 00107393 00137393 00007393 00037393 00007393 00037393 FFF07393 FFF37393
  //   FFD00293 FF900313 00431393 00031393 FFD2A393 00032393 0032A393 00134393 00134393 00034393 00034393
  //   FFF34393 FFF34393 00535393 00035393 40535393 40035393 00136393 00136393 00036393 00036393 FFF36393
  //   FFF36393 00107393 00137393 00007393 00037393 00007393 00037393 FFF07393 FFF37393 FFD00293 00700313
  //   00431393 00031393 FFD2A393 00032393 0032A393 00134393 00134393 00034393 00034393 FFF34393 FFF34393
  //   00535393 00035393 40535393 40035393 00136393 00136393 00036393 00036393 FFF36393 FFF36393 00107393
  //   00137393 00007393 00037393 00007393 00037393 FFF07393 FFF37393
  //   YOUR CPU SHOULD FIT IN HERE!
  //   Instruction Memory
  //   Halts Execution After Constant # of Clock Cycles
  //   Constant
endmodule
