// Logisim project alu.circ as structural Verilog: 1 circuit, main circuit alu
module alu (
  input  [31:0] A,
  input  [31:0] B,
  input  [3:0] ALUSel,
  output [31:0] Result
);

  wire adder_4_cout, ASig, BSig, comparator_1_lt, xor_2_out;
  wire [31:0] add0, adder_2_out, adder_3_out, adder_5_out, and0, bit_extender_1_out, div0, mulh0, mulhu0,
       mult0, multiplexer_2_out, multiplexer_3_out, multiplier_2_cout, multiplier_2_out, not_1_out,
       not_2_out, not_3_out, not_4_out, or0, rem0, sll0, slt0, sra0, srl0, sub0, xor0;

  Adder #(.width(32)) adder_1 (.a(A), .b(B), .out(add0));  // open: cin, cout
  assign and0 = A & B;  // AND_Gate and_1, 32 bits wide
  assign or0 = A | B;  // OR_Gate or_1, 32 bits wide
  assign xor0 = A ^ B;  // XOR_Gate xor_1, 32 bits wide
  Shifter #(.width(32), .shift("lr")) shifter_1 (.in(A), .\dist (B[4:0]), .out(srl0));
  Shifter #(.width(32), .shift("ar")) shifter_2 (.in(A), .\dist (B[4:0]), .out(sra0));
  Shifter #(.width(32)) shifter_3 (.in(A), .\dist (B[4:0]), .out(sll0));
  Comparator #(.width(32)) comparator_1 (.a(A), .b(B), .lt(comparator_1_lt));  // open: gt, eq
  Divider #(.width(32)) divider_1 (.a(A), .b(B), .out(div0), .rem(rem0));  // open: upper
  Multiplier #(.width(32)) multiplier_1 (.a(A), .b(B), .out(mult0), .cout(mulhu0));  // open: cin
  Subtractor #(.width(32)) subtractor_1 (.a(A), .b(B), .out(sub0));  // open: bin, bout
  Multiplexer #(.width(32), .enable("false")) multiplexer_1 (
    .in0({32{1'b0}}), .in1(32'h1), .out(slt0), .sel(comparator_1_lt));
  assign not_1_out = ~A;  // NOT_Gate not_1, 32 bits wide
  assign not_2_out = ~B;  // NOT_Gate not_2, 32 bits wide
  Comparator #(.width(32)) comparator_2 (.a(A), .b({32{1'b0}}), .lt(ASig));  // open: gt, eq
  Comparator #(.width(32)) comparator_3 (.a(B), .b({32{1'b0}}), .lt(BSig));  // open: gt, eq
  Adder #(.width(32)) adder_2 (.a(not_1_out), .b(32'h1), .out(adder_2_out));  // open: cin, cout
  Adder #(.width(32)) adder_3 (.a(not_2_out), .b(32'h1), .out(adder_3_out));  // open: cin, cout
  Multiplexer #(.width(32), .enable("false")) multiplexer_2 (
    .in0(A), .in1(adder_2_out), .out(multiplexer_2_out), .sel(ASig));
  Multiplier #(.width(32)) multiplier_2 (
    .a(multiplexer_2_out), .b(multiplexer_3_out), .out(multiplier_2_out), .cout(multiplier_2_cout));  // open: cin
  Multiplexer #(.width(32), .enable("false")) multiplexer_3 (
    .in0(B), .in1(adder_3_out), .out(multiplexer_3_out), .sel(BSig));
  Multiplexer #(.select(4), .width(32), .enable("false")) multiplexer_4 (
    .in0(add0), .in1(and0), .in2(or0), .in3(xor0), .in4(srl0), .in5(sra0), .in6(sll0), .in7(slt0),
    .in8(div0), .in9(rem0), .in10(mult0), .in11(mulhu0), .in12(sub0), .in13(B), .in14(mulh0), .out(Result),
    .sel(ALUSel));  // open: in15
  assign not_3_out = ~multiplier_2_out;  // NOT_Gate not_3, 32 bits wide
  assign not_4_out = ~multiplier_2_cout;  // NOT_Gate not_4, 32 bits wide
  Adder #(.width(32)) adder_4 (.a(not_3_out), .b(32'h1), .cout(adder_4_cout));  // open: out, cin
  Multiplexer #(.width(32), .enable("false")) multiplexer_5 (
    .in0(multiplier_2_cout), .in1(adder_5_out), .out(mulh0), .sel(xor_2_out));
  Adder #(.width(32)) adder_5 (.a(not_4_out), .b(bit_extender_1_out), .out(adder_5_out));  // open: cin, cout
  xor xor_2 (xor_2_out, ASig, BSig);
  assign bit_extender_1_out = {{31{adder_4_cout}}, adder_4_cout};  // Bit_Extender bit_extender_1

  // Notes on the sheet:
  //   INPUTS to your circuit
  //   DON'T CHANGE THE LOCATIONS OF THE INPUTS AND OUTPUTS!
  //   OUTPUT from your circuit
endmodule
